# Fritzing sketch stepMotor (saved by Fritzing 0.9.0b)
circuit board: 4cm x 4cm
breadboards: 1

parts:
  VCC2 = Battery block 9V
  voltreg = Voltage Regulator - 5V [package="TO220 [THT]"]
  stepper = Stepper Motor - Bipolar
  c1 = Electrolytic Capacitor [capacitance=10μF package="0605 [SMD, electrolytic]"]
  VCC1 = Battery block 9V
  L293D = H-Bridge [package=THT]
  c2 = Electrolytic Capacitor [capacitance=10μF package="0605 [SMD, electrolytic]"]
  atm328 = ATmega328 [package=tqfp]
  resonator = Resonator [frequency="16 Mhz" package=THT]
  serialmon = Stepper Motor - Bipolar

nets:
  GND: VCC2.-, voltreg.GND, c1.-, VCC1.-, L293D.GND1, L293D.GND2, L293D.GND3, L293D.GND4, c2.-, atm328.GND, resonator.GND, serialmon.D
  N1: VCC2.+, voltreg.input_voltage, VCC1.+, L293D.VCC2, c2.+
  N2: voltreg.output_voltage, c1.+, L293D.1_2EN, L293D.3_4EN, L293D.VCC1, atm328.VCC
  N3: stepper.A, L293D.1Y
  N4: stepper.C, L293D.2Y
  N5: stepper.B, L293D.4Y
  N6: stepper.D, L293D.3Y
  N7: L293D.1A, atm328.PB0(ICP)
  N8: L293D.2A, atm328.PB1(OC1A)
  N9: L293D.3A, atm328.PB2(SS_OC1B)
  N10: L293D.4A, atm328.PB3(MOSI_OC2)
  N11: atm328.PB6(XTAL1_TOSC1), resonator.0
  N12: atm328.PB7(XTAL2_TOSC2), resonator.pin_1
  N13: atm328.PC4(ADC4_SDA), serialmon.B
  N14: atm328.PC5(ADC5_SCL), serialmon.C
  N15: atm328.PC6(_RESET), serialmon.A

notes:
  1
  hh & mhj
  +
